# Fritzing sketch schema (saved by Fritzing 1.0.3b)

parts:
  U1 = LuaNode32 / ESP32 [part_number=ESP32S-PIN30]
  S1 = SWITCH-MOMENTARY-2 [package=reed_switch_plastic]

nets:
  N1: U1.D13, S1.2
  N2: U1.3V3, S1.1

custom parts:
  LuaNode32 / ESP32: New Image for LuaNode32 DOIT ESP32 DEVKIT V1. Base parts from LuaNode32 / ESP32 ESP32 based LuaNode32 by G.Noorlander DOIT Esp32 DevKit v1 (30 pins long, 11 pins width) by Werner Rothschopf (modified by vanepp Dec 2018)
